# Fritzing sketch DS18B20_ESP32 (saved by Fritzing 0.9.10b)
breadboards: 1

parts:
  MH-ET_LIVE_ESP32_DEVKIT1 = MH-ET LIVE ESP32 DEVKIT 38 pins
  LED1 = LED - 5mm [color="Red (633nm)" current=0.030 package="5 mm [THT]"]
  R1 = Resistor [tolerance=±5% power=0.25 resistance=220 package=THT]
  R2 = Resistor [tolerance=±5% power=0.25 resistance=220 package=THT]
  LED2 = LED - 5mm [color="Green (565nm)" current=0.030 package="5 mm [THT]"]
  R3 = Resistor [tolerance=±5% power=0.25 resistance=4.7k package=THT]
  U1 = mystery part, 3 pins [chip_label=DS18B20 part_number=DS18B20]

nets:
  N1: MH-ET_LIVE_ESP32_DEVKIT1.3V3, R3.Pin_1, U1.pin3
  N2: MH-ET_LIVE_ESP32_DEVKIT1.IO25, R3.Pin_0, U1.pin2
  N3: MH-ET_LIVE_ESP32_DEVKIT1.GND#64, LED1.cathode, LED2.cathode, U1.pin1
  N4: MH-ET_LIVE_ESP32_DEVKIT1.IO23, R1.Pin_0
  N5: MH-ET_LIVE_ESP32_DEVKIT1.IO22, R2.Pin_0
  N6: LED1.anode, R1.Pin_1
  N7: R2.Pin_1, LED2.anode

custom parts:
  MH-ET LIVE ESP32 DEVKIT 38 pins: http://mh.nodebb.com/topic/2/mh-et-live-esp32-devkit
